# Fritzing sketch Street Light Controller (saved by Fritzing 0.9.3b)
breadboards: 1

parts:
  Part1 = Arduino Nano (Rev3.0)
  R1 = Photocell (LDR) [package=THT]
  R2 = Resistor [tolerance=±5% resistance=1k package="0805 [SMD]"]
  R3 = Resistor [tolerance=±5% resistance=1k package="0805 [SMD]"]
  HC-SR04_Sensor_1 = HC-SR04 Ultrasonic Distance Sensor
  Mod1 = KY-015 Temperature & Humidity Sensor Module [package="Breakout board"]
  LED1 = smd LED [color="White (4500K)" package="0603 [SMD]"]
  VCC1 = Battery
  R4 = Resistor [tolerance=±5% resistance=10k package="2512 [SMD]"]
  LoRa_Module1 = Ra-01 - LoRa Module SX1278 [part_number=SX1278]

nets:
  GND: Part1.GND, R2.Pin_0, HC-SR04_Sensor_1.GND, Mod1.-, LED1.cathode, VCC1.-, LoRa_Module1.GND
  N1: Part1.D2, R3.Pin_1
  N2: Part1.D3, Mod1.S
  N3: Part1.D4, LoRa_Module1.RESET
  N4: Part1.D6, HC-SR04_Sensor_1.ECHO
  N5: Part1.D7, HC-SR04_Sensor_1.TRIG
  N6: Part1.D10, LoRa_Module1.NSS
  N7: Part1.D11/MOSI, LoRa_Module1.MOSI
  N8: Part1.D12/MISO, LoRa_Module1.MISO
  5V: Part1.5V, R1.pin_0, HC-SR04_Sensor_1.VCC, Mod1.Vin
  N9: Part1.A1, R4.Pin_1
  N10: Part1.A0, R1.pin_1, R2.Pin_1
  3V3: Part1.3V3, LoRa_Module1.3.3V
  N11: Part1.D13/SCK, LoRa_Module1.SCK
  N12: R3.Pin_0, LED1.anode
  N13: VCC1.+, R4.Pin_0

notes:
  1200 mAh lithium ion battery

custom parts:
  KY-015 Temperature & Humidity Sensor Module: KY-015 temperature and humidity sensor module, provides a low-latency serial interface to measure humidity and temperature.
  Battery: Your standard 2x 18650 battery pack (7,4 Volts)
  Ra-01 - LoRa Module SX1278: The Ra-01 LoRa Module featuring the SX1278 engine by Semtech. Module by AI-Thinker. Module (Ra-01) specifications from: https://www.banggood.com/Ra-01-Smart-Electronics-SX1278-LoRa-Spread-Spectrum-Wireless-Module-Ultra-Far-10KM-433M-p-1130769.html Description: Power supply: DC1.8-3.7V(3.3V) Chip: SX1278 Frequency: 433Mhz Operating temperature: -40~+85°C On Sheild Description (may vary by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
